# Fritzing sketch RFCT (saved by Fritzing 0.9.3b)
breadboards: 1

parts:
  U1 = LM 358 Dual Op-Amp [package="DIP8 [THT]"]
  R1 = Resistor [tolerance=±1% resistance=3.9k package=THT]
  R2 = Resistor [tolerance=±1% resistance=8.2k package=THT]
  R3 = Resistor [tolerance=±1% resistance=10k package=THT]
  U2 = LM 358 Dual Op-Amp [package="DIP8 [THT]"]
  R4 = Resistor [tolerance=±1% resistance=1k package=THT]
  R5 = Resistor [tolerance=±1% resistance=10k package=THT]
  R6 = Resistor [tolerance=±1% resistance=1k package=THT]
  C1 = Ceramic Capacitor [capacitance=100nF package="100 mil [THT, multilayer]"]
  C2 = Ceramic Capacitor [capacitance=100nF package="100 mil [THT, multilayer]"]
  C3 = Ceramic Capacitor [capacitance=100nF package="100 mil [THT, multilayer]"]
  C4 = Ceramic Capacitor [capacitance=100nF package="100 mil [THT, multilayer]"]

nets:
  N1: U1.connector0, U1.connector1, U2.connector2, C1.0
  N2: U1.connector2, U1.connector4, R1.Pin_0, R2.Pin_0
  N3: U1.connector3, R1.Pin_1, U2.connector3
  N4: U1.connector5, U1.connector6, U2.connector4, C2.1
  N5: U1.connector7, R2.Pin_1, U2.connector7
  N6: R3.Pin_0, U2.connector0, C3.1
  N7: R3.Pin_1, U2.connector1, R4.Pin_0, C1.1, C3.0
  N8: U2.connector5, R5.Pin_1, R6.Pin_0, C2.0, C4.1
  N9: U2.connector6, R5.Pin_0, C4.0
